# Fritzing sketch ProjetoMicrocontroladores (saved by Fritzing 0.9.3b)
breadboards: 1

parts:
  A1 = drv-1012
  Componente1 = Arduino Mega 2560 (Rev3)
  M1 = DC Motor
  M2 = DC Motor
  A2 = Adafruit v1.2 motor shield
  M3 = DC Motor
  M4 = DC Motor
  M5 = DC Motor

nets:
  N1: A1.Pin_1, A1.Pin_7
  N2: A1.Pin_3, A1.Pin_5, Componente1.GND
  N3: A1.Pin_4, A2.Pin_59, A2.Pin_68
  N4: A1.Pin_8, A2.Pin_63, A2.Pin_70
  N5: A1.Pin_9, M2.pin_2
  N6: A1.Pin_10, M2.pin_1
  N7: M1.pin_1, A2.Pin_48
  N8: M1.pin_2, A2.Pin_47
  N9: A2.Pin_1, M3.pin_2
  N10: A2.Pin_2, M3.pin_1
  N11: A2.Pin_4, M5.pin_2
  N12: A2.Pin_5, M5.pin_1
  N13: A2.Pin_44, M4.pin_2
  N14: A2.Pin_45, M4.pin_1

notes:
  Liquidificador
  escova
  CD
  Impressora
  Máquina de costura

custom parts:
  drv-1012: .The BTS7960 is a fully integrated high current H bridge module for motor drive applications.
  Adafruit v1.2 motor shield: Adafruit v1.2 motor shield.
